# Fritzing sketch Schematic (saved by Fritzing 0.9.2b)
breadboards: 2

parts:
  U1 = NodeMCU V3.0
  LED2 = LED - 3mm [color="Red (635nm)" package="3 mm [THT]"]
  C2 = Capacitor Polarized [package=panasonic_c]
  LED3 = LED - 3mm [color="Red (635nm)" package="3 mm [THT]"]
  LED4 = LED - 3mm [color="Yellow (595nm)" package="3 mm [THT]"]
  Led15 = LED - 3mm [color="Red (635nm)" package="3 mm [THT]"]
  Led16 = LED - 3mm [color="Red (635nm)" package="3 mm [THT]"]
  LED17 = LED - 3mm [color="Red (635nm)" package="3 mm [THT]"]
  LED6 = LED - 3mm [color="Yellow (595nm)" package="3 mm [THT]"]
  LED8 = LED - 3mm [color="Yellow (595nm)" package="3 mm [THT]"]
  LED11 = LED - 3mm [color="Yellow (595nm)" package="3 mm [THT]"]
  LED13 = LED - 3mm [color="Yellow (595nm)" package="3 mm [THT]"]
  LED12 = LED - 3mm [color="Green (555nm)" package="3 mm [THT]"]
  LED10 = LED - 3mm [color="Green (555nm)" package="3 mm [THT]"]
  LED9 = LED - 3mm [color="Blue (430nm)" package="3 mm [THT]"]
  LED5 = LED - 3mm [color="Green (555nm)" package="3 mm [THT]"]
  LED7 = LED - 3mm [color="Green (555nm)" package="3 mm [THT]"]
  C3 = Capacitor [package=cap-pth-small2]
  Q3 = TRANSISTOR_NPN [package=to-92-ammo]
  Q4 = TRANSISTOR_NPN [package=to-92-ammo]
  Q6 = TRANSISTOR_NPN [package=to-92-ammo]
  Q7 = TRANSISTOR_NPN [package=to-92-ammo]
  PhotoResistor = Photocell (LDR) [package=THT]
  USBTTL1 = USB TTL Serial Cable
  PIR1 = PIR sensor
  R2 = Resistor [tolerance=±5% resistance=22k package=THT]
  LED1 = LED - 3mm [color="Red (635nm)" package="3 mm [THT]"]
  Q1 = TRANSISTOR_NPN [package=to-92-ammo]
  R_Led3 = Resistor [tolerance=±5% resistance=160 package=THT]
  R_Q2 = Resistor [tolerance=±5% resistance=4.7k package=THT]
  R_Q1 = Resistor [tolerance=±5% resistance=4.7k package=THT]
  R_Q3 = Resistor [tolerance=±5% resistance=4.7k package=THT]
  R_Q4 = Resistor [tolerance=±5% resistance=4.7k package=THT]
  R_Q5 = Resistor [tolerance=±5% resistance=4.7k package=THT]
  R_Q6 = Resistor [tolerance=±5% resistance=4.7k package=THT]
  R_Q7 = Resistor [tolerance=±5% resistance=4.7k package=THT]
  R_Led1 = Resistor [tolerance=±5% resistance=160 package=THT]
  R_Led4 = Resistor [tolerance=±5% resistance=160 package=THT]
  R_Led6 = Resistor [tolerance=±5% resistance=160 package=THT]
  R_Led7 = Resistor [tolerance=±5% resistance=160 package=THT]
  R_Led8 = Resistor [tolerance=±5% resistance=160 package=THT]
  R_Led10 = Resistor [tolerance=±5% resistance=160 package=THT]
  R_Led13 = Resistor [tolerance=±5% resistance=160 package=THT]
  R_Led14 = Resistor [tolerance=±5% resistance=160 package=THT]
  R_Led15 = Resistor [tolerance=±5% resistance=160 package=THT]
  R_Led16 = Resistor [tolerance=±5% resistance=160 power=2W package=THT]
  R_Led5 = Resistor [tolerance=±5% resistance=160 package=THT]
  R_Led9 = Resistor [tolerance=±5% resistance=100 package=THT]
  R_Led2 = Resistor [tolerance=±5% resistance=160 package=THT]
  R_Led17 = Resistor [tolerance=±5% resistance=160 package=THT]
  Q2 = TRANSISTOR_NPN [package=to-92-ammo]
  Q5 = TRANSISTOR_NPN [package=to-92-ammo]
  LED14 = LED - 3mm [color="Green (555nm)" package="3 mm [THT]"]
  R_Led11 = Resistor [tolerance=±5% resistance=160 package=THT]
  R_Led12 = Resistor [tolerance=±5% resistance=160 package=THT]
  LEDSMD2 = LEDs [package=led-1206]
  LEDSMD1 = LEDs [package=led-1206]
  QSMD = TRANSISTOR_NPN [package=to-92-ammo]
  R_SMD2 = Resistor [tolerance=±5% resistance=33 power=2W package="2010 [SMD]"]
  R_SMD1 = Resistor [tolerance=±5% resistance=33 power=2W package="2010 [SMD]"]
  R_QSMD = Resistor [tolerance=±5% resistance=4.7k package=THT]

nets:
  N1: U1.D0, PIR1.SIG
  N2: U1.D1, R_Q1.Pin_1
  N3: U1.D2, R_Q2.Pin_1
  N4: U1.D3, R_Q3.Pin_1
  N5: U1.D4, R_Q4.Pin_1
  N6: U1.D5, R_Q5.Pin_1
  N7: U1.D6, R_Q6.Pin_1
  N8: U1.D7, R_Q7.Pin_1
  N9: U1.D8, R_QSMD.Pin_1
  VIN: U1.Vin, LED2.anode, C2.+, LED3.anode, LED4.anode, Led15.anode, Led16.anode, LED17.anode, LED6.anode, LED8.anode, LED11.anode, LED13.anode, LED12.anode, LED10.anode, LED9.anode, LED5.anode, LED7.anode, C3.2, USBTTL1.5V, PIR1.VDD, LED1.anode, LED14.anode, LEDSMD2.A, LEDSMD1.A
  GND: U1.GND, C2.-, C3.1, Q3.E, Q4.E, Q6.E, Q7.E, USBTTL1.GND, PIR1.GND, R2.Pin_0, Q1.E, Q2.E, Q5.E, QSMD.E
  N10: U1.3V3, PhotoResistor.pin_1
  N11: U1.A0, PhotoResistor.pin_0, R2.Pin_1
  N12: LED2.cathode, R_Led2.Pin_1
  N13: LED3.cathode, R_Led3.Pin_1
  N14: LED4.cathode, R_Led4.Pin_1
  N15: Led15.cathode, R_Led15.Pin_1
  N16: Led16.cathode, R_Led16.Pin_1
  N17: LED17.cathode, R_Led17.Pin_1
  N18: LED6.cathode, R_Led6.Pin_1
  N19: LED8.cathode, R_Led8.Pin_1
  N20: LED11.cathode, R_Led11.Pin_1
  N21: LED13.cathode, R_Led13.Pin_1
  N22: LED12.cathode, R_Led12.Pin_1
  N23: LED10.cathode, R_Led10.Pin_1
  N24: LED9.cathode, R_Led9.Pin_1
  N25: LED5.cathode, R_Led5.Pin_1
  N26: LED7.cathode, R_Led7.Pin_1
  N27: Q3.B, R_Q3.Pin_0
  N28: Q3.C, R_Led7.Pin_0, R_Led5.Pin_0
  N29: Q4.B, R_Q4.Pin_0
  N30: Q4.C, R_Led9.Pin_0
  N31: Q6.B, R_Q6.Pin_0
  N32: Q6.C, R_Led13.Pin_0, R_Led11.Pin_0
  N33: Q7.B, R_Q7.Pin_0
  N34: Q7.C, R_Led15.Pin_0, R_Led16.Pin_0, R_Led17.Pin_0
  N35: LED1.cathode, R_Led1.Pin_1
  N36: Q1.B, R_Q1.Pin_0
  N37: Q1.C, R_Led3.Pin_0, R_Led1.Pin_0, R_Led2.Pin_0
  N38: R_Q2.Pin_0, Q2.B
  N39: R_Q5.Pin_0, Q5.B
  N40: R_Led4.Pin_0, R_Led6.Pin_0, R_Led8.Pin_0, Q2.C
  N41: R_Led10.Pin_0, R_Led14.Pin_0, Q5.C, R_Led12.Pin_0
  N42: R_Led14.Pin_1, LED14.cathode
  N43: LEDSMD2.C, R_SMD2.Pin_0
  N44: LEDSMD1.C, R_SMD1.Pin_0
  N45: QSMD.B, R_QSMD.Pin_0
  N46: QSMD.C, R_SMD2.Pin_1, R_SMD1.Pin_1

custom parts:
  NodeMCU V3.0: ESP8266 based NodeMCU
